# Fritzing sketch ViaShift (saved by Fritzing 0.9.6b)
circuit board: 8.46667cm x 5.64444cm
breadboards: 1

parts:
  Part1 = Arduino Uno (Rev3)
  DI1 = 7-Segment LED Display [package=THT]
  U1 = 74HC595 [package="DIP16 [THT]"]
  R4 = Resistor [tolerance=±5% resistance=220 power=0.25 package=THT]
  R3 = Resistor [tolerance=±5% resistance=220 power=0.25 package=THT]
  R5 = Resistor [tolerance=±5% resistance=220 power=0.25 package=THT]
  R6 = Resistor [tolerance=±5% resistance=220 power=0.25 package=THT]
  R7 = Resistor [tolerance=±5% resistance=220 power=0.25 package=THT]
  R8 = Resistor [tolerance=±5% resistance=220 power=0.25 package=THT]
  R9 = Resistor [tolerance=±5% resistance=220 power=0.25 package=THT]
  R10 = Resistor [tolerance=±5% resistance=220 power=0.25 package=THT]
  Power_plug1 = Power plug

nets:
  N1: Part1.D5_PWM, U1.SH_CP
  N2: Part1.D6_PWM, U1.DS
  N3: Part1.D7, U1.ST_CP
  VCC: Part1.5V, U1.VCC, Power_plug1.VCC
  GND: Part1.GND, DI1.commAnode#7, U1.GND, U1.MR, U1.OE, Power_plug1.GND
  N4: DI1.cathodeE, R10.Pin_1
  N5: DI1.cathodeD, R9.Pin_1
  N6: DI1.cathodeC, R8.Pin_1
  N7: DI1.cathodeDP, R7.Pin_1
  N8: DI1.cathodeB, R5.Pin_0
  N9: DI1.cathodeA, R3.Pin_1
  N10: DI1.cathodeF, R4.Pin_1
  N11: DI1.cathodeG, R6.Pin_1
  N12: U1.Q1, R5.Pin_1
  N13: U1.Q2, R8.Pin_0
  N14: U1.Q3, R9.Pin_0
  N15: U1.Q4, R10.Pin_0
  N16: U1.Q5, R4.Pin_0
  N17: U1.Q6, R6.Pin_0
  N18: U1.Q7, R7.Pin_0
  N19: U1.Q0, R3.Pin_0
